# Fritzing sketch Flow (saved by Fritzing 0.9.3b)

parts:
  V2 = DC Power [voltage=5]  # not connected
  A1 = yf-s401 flow sensor [package=THT]
  Part1 = Real Time Clock Module - DS1307 RTC Breakout Board
  microSD1 = MicroSD Card Module
  U1 = ESP32-38PinWide [part_number=ESP32-38PinWide]

nets:
  5V: A1.pin1, Part1.5V, U1.VIN
  GND: A1.pin2, Part1.GND, microSD1.GND, U1.GND
  N1: A1.pin3, U1.GPIO27
  N2: Part1.SCL, U1.GPIO22
  N3: Part1.SDA, U1.GPIO21
  N4: microSD1.VCC, U1.3.3
  N5: microSD1.MISO, U1.GPIO19
  N6: microSD1.MOSI, U1.GPIO23
  N7: microSD1.SCK, U1.GPIO18
  N8: microSD1.CS, U1.GPIO5

notes:
  +5V

custom parts:
  yf-s401 flow sensor: Flow sensors sit in line with your water line, and uses a pinwheel sensor to measure how much liquid has moved through it.
  ESP32-38PinWide: Generic 38-Pin ESP32 with wide format (only access to one side of pins on a breadboard) based on Stephen Lilley's HiLetgo ESP-WROOM-32 ESP32 ESP-32S Development Board.
